// Logisim project Forward.circ as structural Verilog: 1 circuit, main circuit main
module main (
  input  EX_MEM_RegWrite,
  input  MEM_WB_RegWrite,
  input  EX_MEM_RegisterRd_0,
  input  EX_MEM_RegisterRd_1,
  input  EX_MEM_RegisterRd_2,
  input  EX_MEM_RegisterRd_3,
  input  EX_MEM_RegisterRd_4,
  input  ID_EX_RegisterRs_0,
  input  ID_EX_RegisterRs_1,
  input  ID_EX_RegisterRs_2,
  input  ID_EX_RegisterRs_3,
  input  ID_EX_RegisterRs_4,
  input  ID_EX_RegisterRt_0,
  input  ID_EX_RegisterRt_1,
  input  ID_EX_RegisterRt_2,
  input  ID_EX_RegisterRt_3,
  input  ID_EX_RegisterRt_4,
  input  MEM_WB_RegisterRd_0,
  input  MEM_WB_RegisterRd_1,
  input  MEM_WB_RegisterRd_2,
  input  MEM_WB_RegisterRd_3,
  input  MEM_WB_RegisterRd_4,
  output ForwardA_0,
  output ForwardA_1,
  output ForwardB_0,
  output ForwardB_1
);

  wire EX_MEM_RegisterRd____0_out, EX_MEM_RegisterRd___ID_EX_RegisterRs_out,
       EX_MEM_RegisterRd___ID_EX_RegisterRt_out, MEM_WB_RegisterRd____0_out,
       MEM_WB_RegisterRd___ID_EX_RegisterRs_out, MEM_WB_RegisterRd___ID_EX_RegisterRt_out, nand_1_out,
       nand_2_out, not_1_out, xnor_1_out, xnor_2_out, xnor_3_out, xnor_4_out, xnor_5_out, xnor_6_out,
       xnor_7_out, xnor_8_out, xnor_9_out, xnor_10_out, xnor_11_out, xnor_12_out, xnor_13_out, xnor_14_out,
       xnor_15_out, xnor_16_out, xnor_17_out, xnor_18_out, xnor_19_out, xnor_20_out;

  or EX_MEM_RegisterRd____0 (EX_MEM_RegisterRd____0_out, EX_MEM_RegisterRd_0, EX_MEM_RegisterRd_1, EX_MEM_RegisterRd_2, EX_MEM_RegisterRd_3, EX_MEM_RegisterRd_4);
  xnor xnor_1 (xnor_1_out, EX_MEM_RegisterRd_0, ID_EX_RegisterRs_0);
  xnor xnor_2 (xnor_2_out, EX_MEM_RegisterRd_1, ID_EX_RegisterRs_1);
  xnor xnor_3 (xnor_3_out, EX_MEM_RegisterRd_2, ID_EX_RegisterRs_2);
  and EX_MEM_RegisterRd___ID_EX_RegisterRs (EX_MEM_RegisterRd___ID_EX_RegisterRs_out, xnor_1_out, xnor_2_out, xnor_3_out, xnor_4_out, xnor_5_out);
  xnor xnor_4 (xnor_4_out, EX_MEM_RegisterRd_3, ID_EX_RegisterRs_3);
  xnor xnor_5 (xnor_5_out, EX_MEM_RegisterRd_4, ID_EX_RegisterRs_4);
  xnor xnor_6 (xnor_6_out, EX_MEM_RegisterRd_0, ID_EX_RegisterRt_0);
  xnor xnor_7 (xnor_7_out, EX_MEM_RegisterRd_1, ID_EX_RegisterRt_1);
  xnor xnor_8 (xnor_8_out, EX_MEM_RegisterRd_2, ID_EX_RegisterRt_2);
  and EX_MEM_RegisterRd___ID_EX_RegisterRt (EX_MEM_RegisterRd___ID_EX_RegisterRt_out, xnor_6_out, xnor_7_out, xnor_8_out, xnor_9_out, xnor_10_out);
  xnor xnor_9 (xnor_9_out, EX_MEM_RegisterRd_3, ID_EX_RegisterRt_3);
  xnor xnor_10 (xnor_10_out, EX_MEM_RegisterRd_4, ID_EX_RegisterRt_4);
  or MEM_WB_RegisterRd____0 (MEM_WB_RegisterRd____0_out, MEM_WB_RegisterRd_0, MEM_WB_RegisterRd_1, MEM_WB_RegisterRd_2, MEM_WB_RegisterRd_3, MEM_WB_RegisterRd_4);
  xnor xnor_11 (xnor_11_out, MEM_WB_RegisterRd_0, ID_EX_RegisterRs_0);
  xnor xnor_12 (xnor_12_out, MEM_WB_RegisterRd_1, ID_EX_RegisterRs_1);
  xnor xnor_13 (xnor_13_out, MEM_WB_RegisterRd_2, ID_EX_RegisterRs_2);
  and MEM_WB_RegisterRd___ID_EX_RegisterRs (MEM_WB_RegisterRd___ID_EX_RegisterRs_out, xnor_11_out, xnor_12_out, xnor_13_out, xnor_15_out, xnor_14_out);
  xnor xnor_14 (xnor_14_out, MEM_WB_RegisterRd_4, ID_EX_RegisterRs_4);
  xnor xnor_15 (xnor_15_out, MEM_WB_RegisterRd_3, ID_EX_RegisterRs_3);
  xnor xnor_16 (xnor_16_out, MEM_WB_RegisterRd_0, ID_EX_RegisterRt_0);
  xnor xnor_17 (xnor_17_out, MEM_WB_RegisterRd_1, ID_EX_RegisterRt_1);
  xnor xnor_18 (xnor_18_out, MEM_WB_RegisterRd_2, ID_EX_RegisterRt_2);
  and MEM_WB_RegisterRd___ID_EX_RegisterRt (MEM_WB_RegisterRd___ID_EX_RegisterRt_out, xnor_16_out, xnor_17_out, xnor_18_out, xnor_19_out, xnor_20_out);
  xnor xnor_19 (xnor_19_out, MEM_WB_RegisterRd_3, ID_EX_RegisterRt_3);
  not not_1 (not_1_out, EX_MEM_RegisterRd___ID_EX_RegisterRs_out);
  xnor xnor_20 (xnor_20_out, MEM_WB_RegisterRd_4, ID_EX_RegisterRt_4);
  nand nand_1 (nand_1_out, EX_MEM_RegisterRd____0_out, not_1_out, EX_MEM_RegWrite);
  nand nand_2 (nand_2_out, EX_MEM_RegisterRd____0_out, EX_MEM_RegisterRd___ID_EX_RegisterRt_out, EX_MEM_RegWrite);
  and and_1 (ForwardA_0, MEM_WB_RegisterRd___ID_EX_RegisterRs_out, MEM_WB_RegisterRd____0_out, nand_1_out, MEM_WB_RegWrite);
  and and_2 (ForwardA_1, EX_MEM_RegisterRd____0_out, EX_MEM_RegisterRd___ID_EX_RegisterRs_out, EX_MEM_RegWrite);
  and and_3 (ForwardB_0, MEM_WB_RegisterRd____0_out, MEM_WB_RegisterRd___ID_EX_RegisterRt_out, nand_2_out, MEM_WB_RegWrite);
  and and_4 (ForwardB_1, EX_MEM_RegisterRd____0_out, EX_MEM_RegisterRd___ID_EX_RegisterRt_out, EX_MEM_RegWrite);
endmodule
